// Logisim project serial_july_2025.circ as structural Verilog: 8 circuits, main circuit main
module main (
);

  wire clock_1_out, clock_3_out, clock_4_out, mul_1_out_3, shift_register_1_p2, shift_register_1_p3,
       shift_register_1_p4, shift_register_1_p5, shift_register_1_p6, shift_register_1_p7,
       shift_register_1_p8, shift_register_1_p9, shift_register_1_p10, shift_register_1_p11,
       shift_register_1_p12, shift_register_1_p13, shift_register_1_p14, shift_register_1_p15,
       shift_register_1_p16, shift_register_1_p17, shift_register_2_q0, shift_register_2_q7,
       shift_register_2_q8, shift_register_2_q15, shift_register_2_q16, shift_register_2_q23,
       shift_register_2_q24, shift_register_2_q31, shift_register_3_out, shift_register_4_q31, undriven,
       var_2_out_2;
  wire [7:0] dbg_1_out_2, dbg_2_out_2, dbg_3_out_2;

  // Probe on 8'h2
  // Probe on 8'h2
  // Probe on 8'h2
  // Probe on 8'h2
  Clock clock_1 (.out(clock_1_out));
  \var  var_1 (.in_1(8'h2));  // open: out_2
  \var  var_2 (.in_1(8'h2), .out_2(var_2_out_2));
  // Shift_Register #(.length(32)) shift_register_1: pin names not known; wires that end beside it: var_2_out_2, shift_register_1_p2, shift_register_1_p3, shift_register_1_p4, shift_register_1_p5, shift_register_1_p6, shift_register_1_p7, shift_register_1_p8, shift_register_1_p9, shift_register_1_p10, shift_register_1_p11, shift_register_1_p12, shift_register_1_p13, shift_register_1_p14, shift_register_1_p15, shift_register_1_p16, shift_register_1_p17
  Clock clock_2 (.out(shift_register_1_p2));
  Shift_Register #(.length(32)) shift_register_2 (
    .in(undriven), .clk(clock_1_out), .q0(shift_register_2_q0), .q7(shift_register_2_q7),
    .q8(shift_register_2_q8), .q15(shift_register_2_q15), .q16(shift_register_2_q16),
    .q23(shift_register_2_q23), .q24(shift_register_2_q24), .q31(shift_register_2_q31));  // open: shift, out, load, clr, d0, d1, q1, d2, q2, d3, q3, d4, q4, d5, q5, d6, q6, d7, d8, d9, q9, d10, q10, d11, q11, d12, q12, d13, q13, d14, q14, d15, d16, d17, q17, d18, q18, d19, q19, d20, q20, d21, q21, d22, q22, d23, d24, d25, q25, d26, q26, d27, q27, d28, q28, d29, q29, d30, q30, d31
  dbg dbg_1 (.in_1(undriven), .out_2(dbg_1_out_2));
  // Probe on dbg_1_out_2
  mul mul_1 (.out_3(mul_1_out_3), .A(shift_register_3_out), .B(var_2_out_2));
  Shift_Register #(.length(7)) shift_register_3 (
    .in(mul_1_out_3), .clk(clock_3_out), .out(shift_register_3_out));  // open: shift, load, clr, d0, q0, d1, q1, d2, q2, d3, q3, d4, q4, d5, q5, d6, q6
  Clock clock_3 (.out(clock_3_out));
  // Probe on dbg_2_out_2
  dbg dbg_2 (.in_1(var_2_out_2), .out_2(dbg_2_out_2));
  Shift_Register #(.length(32)) shift_register_4 (
    .in(mul_1_out_3), .clk(clock_4_out), .q0(shift_register_1_p5), .q7(shift_register_1_p7),
    .q8(shift_register_1_p9), .q15(shift_register_1_p11), .q16(shift_register_1_p13),
    .q23(shift_register_1_p15), .q24(shift_register_1_p17), .q31(shift_register_4_q31));  // open: shift, out, load, clr, d0, d1, q1, d2, q2, d3, q3, d4, q4, d5, q5, d6, q6, d7, d8, d9, q9, d10, q10, d11, q11, d12, q12, d13, q13, d14, q14, d15, d16, d17, q17, d18, q18, d19, q19, d20, q20, d21, q21, d22, q22, d23, d24, d25, q25, d26, q26, d27, q27, d28, q28, d29, q29, d30, q30, d31
  Clock clock_4 (.out(clock_4_out));
  // Probe on 8'h97
  // Probe on dbg_3_out_2
  dbg dbg_3 (.in_1(shift_register_3_out), .out_2(dbg_3_out_2));
  // Probe on 8'h97
  add add_1 ();  // open: in_1, in_2, out_3
endmodule

module \var  (
  input  [7:0] in_1,
  output out_2
);

  wire and_1_out, clock_1_out;
  wire [2:0] counter_1_q;

  Counter #(.width(3), .max('h7)) counter_1 (.Q(counter_1_q), .clk(clock_1_out));  // open: load, D, count, carry, clr
  Clock clock_1 (.out(clock_1_out));
  and and_1 (and_1_out, ~counter_1_q[0], ~counter_1_q[1], ~counter_1_q[2]);  // AND_Gate
  Shift_Register shift_register_1 (
    .clk(clock_1_out), .out(out_2), .load(and_1_out), .d0(in_1[7]), .d1(in_1[6]), .d2(in_1[5]), .d3(in_1[4]),
    .d4(in_1[3]), .d5(in_1[2]), .d6(in_1[1]), .d7(in_1[0]));  // open: shift, in, clr, q0, q1, q2, q3, q4, q5, q6, q7
endmodule

module dbg (
  input  in_1,
  output [7:0] out_2
);

  wire and_1_out, clock_1_out, d_ff_1_q;
  wire [2:0] counter_1_q;
  wire [7:0] shift_register_1_q7;

  Counter #(.width(3), .max('h7)) counter_1 (.Q(counter_1_q), .clk(clock_1_out));  // open: load, D, count, carry, clr
  Shift_Register shift_register_1 (
    .in(in_1), .clk(clock_1_out), .q0(shift_register_1_q7[7]), .q1(shift_register_1_q7[6]),
    .q2(shift_register_1_q7[5]), .q3(shift_register_1_q7[4]), .q4(shift_register_1_q7[3]),
    .q5(shift_register_1_q7[2]), .q6(shift_register_1_q7[1]), .q7(shift_register_1_q7[0]));  // open: shift, out, load, clr, d0, d1, d2, d3, d4, d5, d6, d7
  Clock clock_1 (.out(clock_1_out));
  and and_1 (and_1_out, ~counter_1_q[0], ~counter_1_q[1], ~counter_1_q[2]);  // AND_Gate
  D_Flip_Flop d_ff_1 (.clk(clock_1_out), .D(and_1_out), .Q(d_ff_1_q));  // open: Qn, preset, en, reset
  Register register_1 (.D(shift_register_1_q7), .en(d_ff_1_q), .Q(out_2), .clk(clock_1_out));  // open: clr
endmodule

module add (
  input  in_1,
  input  in_2,
  output out_3
);

  wire and_1_out, and_2_out, and_3_out, and_4_out, clock_1_out, d_ff_1_q, or_1_out, xor_1_out;
  wire [2:0] counter_1_q;

  xor xor_1 (xor_1_out, in_1, in_2);
  and and_1 (and_1_out, in_2, in_1);
  Counter #(.width(3), .max('h7)) counter_1 (.Q(counter_1_q), .clk(clock_1_out));  // open: load, D, count, carry, clr
  Clock clock_1 (.out(clock_1_out));
  xor xor_2 (out_3, d_ff_1_q, xor_1_out);
  and and_2 (and_2_out, xor_1_out, d_ff_1_q);
  or or_1 (or_1_out, and_2_out, and_1_out);
  and and_3 (and_3_out, ~counter_1_q[0], ~counter_1_q[1], ~counter_1_q[2]);  // AND_Gate
  and and_4 (and_4_out, or_1_out, ~and_3_out);  // AND_Gate
  D_Flip_Flop d_ff_1 (.clk(clock_1_out), .D(and_4_out), .Q(d_ff_1_q), .preset(1'b0), .en(1'b1));  // open: Qn, reset
endmodule

module main2 (
);

  wire add_1_out_3, add_2_out_3, add_3_out_3, clock_1_out, clock_3_out, shift_register_1_p2,
       shift_register_1_p3, shift_register_1_p4, shift_register_1_p5, shift_register_1_p6,
       shift_register_1_p7, shift_register_1_p8, shift_register_1_p9, shift_register_1_p10,
       shift_register_1_p11, shift_register_1_p12, shift_register_1_p13, shift_register_1_p14,
       shift_register_1_p15, shift_register_1_p16, shift_register_1_p17, shift_register_2_q0,
       shift_register_2_q7, shift_register_2_q8, shift_register_2_q15, shift_register_2_q16,
       shift_register_2_q23, shift_register_2_q24, shift_register_2_q31, shift_register_3_q31, var_1_out_2,
       var_2_out_2, var_3_out_2, var_4_out_2;
  wire [7:0] dbg_1_out_2, dbg_2_out_2, dbg_3_out_2;

  // Probe on 8'h5
  \var  var_1 (.in_1(8'h5), .out_2(var_1_out_2));
  // Probe on 8'h5
  // Probe on 8'h7a
  \var  var_2 (.in_1(8'h7a), .out_2(var_2_out_2));
  // Probe on 8'h7a
  // Probe on 8'h81
  \var  var_3 (.in_1(8'h81), .out_2(var_3_out_2));
  // Probe on 8'h81
  // Probe on {8{1'b1}}
  \var  var_4 (.in_1({8{1'b1}}), .out_2(var_4_out_2));
  // Probe on {8{1'b1}}
  Clock clock_1 (.out(clock_1_out));
  add add_1 (.in_1(var_1_out_2), .in_2(var_2_out_2), .out_3(add_1_out_3));
  add add_2 (.in_1(var_3_out_2), .in_2(var_4_out_2), .out_3(add_2_out_3));
  // Shift_Register #(.length(32)) shift_register_1: pin names not known; wires that end beside it: add_2_out_3, shift_register_1_p2, shift_register_1_p3, shift_register_1_p4, shift_register_1_p5, shift_register_1_p6, shift_register_1_p7, shift_register_1_p8, shift_register_1_p9, shift_register_1_p10, shift_register_1_p11, shift_register_1_p12, shift_register_1_p13, shift_register_1_p14, shift_register_1_p15, shift_register_1_p16, shift_register_1_p17
  Clock clock_2 (.out(shift_register_1_p2));
  Shift_Register #(.length(32)) shift_register_2 (
    .in(add_1_out_3), .clk(clock_1_out), .q0(shift_register_2_q0), .q7(shift_register_2_q7),
    .q8(shift_register_2_q8), .q15(shift_register_2_q15), .q16(shift_register_2_q16),
    .q23(shift_register_2_q23), .q24(shift_register_2_q24), .q31(shift_register_2_q31));  // open: shift, out, load, clr, d0, d1, q1, d2, q2, d3, q3, d4, q4, d5, q5, d6, q6, d7, d8, d9, q9, d10, q10, d11, q11, d12, q12, d13, q13, d14, q14, d15, d16, d17, q17, d18, q18, d19, q19, d20, q20, d21, q21, d22, q22, d23, d24, d25, q25, d26, q26, d27, q27, d28, q28, d29, q29, d30, q30, d31
  dbg dbg_1 (.in_1(add_1_out_3), .out_2(dbg_1_out_2));
  // Probe on dbg_1_out_2
  dbg dbg_2 (.in_1(add_3_out_3), .out_2(dbg_2_out_2));
  add add_3 (.in_1(add_1_out_3), .in_2(add_2_out_3), .out_3(add_3_out_3));
  // Probe on dbg_2_out_2
  // Probe on dbg_3_out_2
  dbg dbg_3 (.in_1(add_2_out_3), .out_2(dbg_3_out_2));
  Shift_Register #(.length(32)) shift_register_3 (
    .in(add_3_out_3), .clk(clock_3_out), .q0(shift_register_1_p5), .q7(shift_register_1_p7),
    .q8(shift_register_1_p9), .q15(shift_register_1_p11), .q16(shift_register_1_p13),
    .q23(shift_register_1_p15), .q24(shift_register_1_p17), .q31(shift_register_3_q31));  // open: shift, out, load, clr, d0, d1, q1, d2, q2, d3, q3, d4, q4, d5, q5, d6, q6, d7, d8, d9, q9, d10, q10, d11, q11, d12, q12, d13, q13, d14, q14, d15, d16, d17, q17, d18, q18, d19, q19, d20, q20, d21, q21, d22, q22, d23, d24, d25, q25, d26, q26, d27, q27, d28, q28, d29, q29, d30, q30, d31
  Clock clock_3 (.out(clock_3_out));
  // Probe on 8'hf5
  // Probe on 8'hf5
endmodule

module superadder (
  input  [7:0] in_1,
  input  [7:0] in_2,
  input  [7:0] in_3,
  input  [7:0] in_4,
  input  [7:0] in_5,
  input  [7:0] in_6,
  input  [7:0] in_7,
  input  [7:0] in_8,
  input  [7:0] in_9,
  input  [7:0] in_10,
  input  [7:0] in_11,
  input  [7:0] in_12,
  input  [7:0] in_13,
  input  [7:0] in_14,
  input  [7:0] in_15,
  input  [7:0] in_16,
  output [7:0] out_17
);

  wire add_1_out_3, add_2_out_3, add_3_out_3, add_4_out_3, add_5_out_3, add_6_out_3, add_7_out_3,
       add_8_out_3, add_9_out_3, add_10_out_3, add_11_out_3, add_12_out_3, add_13_out_3, add_14_out_3,
       add_15_out_3, var_1_out_2, var_2_out_2, var_3_out_2, var_4_out_2, var_5_out_2, var_6_out_2,
       var_7_out_2, var_8_out_2, var_9_out_2, var_10_out_2, var_11_out_2, var_12_out_2, var_13_out_2,
       var_14_out_2, var_15_out_2, var_16_out_2;
  wire [7:0] dbg_1_out_2, dbg_2_out_2, dbg_4_out_2;

  \var  var_1 (.in_1(in_1), .out_2(var_1_out_2));
  add add_1 (.in_1(var_1_out_2), .in_2(var_2_out_2), .out_3(add_1_out_3));
  \var  var_2 (.in_1(in_2), .out_2(var_2_out_2));
  \var  var_3 (.in_1(in_3), .out_2(var_3_out_2));
  add add_2 (.in_1(var_3_out_2), .in_2(var_4_out_2), .out_3(add_2_out_3));
  \var  var_4 (.in_1(in_4), .out_2(var_4_out_2));
  \var  var_5 (.in_1(in_5), .out_2(var_5_out_2));
  add add_3 (.in_1(var_5_out_2), .in_2(var_6_out_2), .out_3(add_3_out_3));
  \var  var_6 (.in_1(in_6), .out_2(var_6_out_2));
  \var  var_7 (.in_1(in_7), .out_2(var_7_out_2));
  add add_4 (.in_1(var_7_out_2), .in_2(var_8_out_2), .out_3(add_4_out_3));
  \var  var_8 (.in_1(in_8), .out_2(var_8_out_2));
  \var  var_9 (.in_1(in_9), .out_2(var_9_out_2));
  add add_5 (.in_1(var_9_out_2), .in_2(var_10_out_2), .out_3(add_5_out_3));
  \var  var_10 (.in_1(in_10), .out_2(var_10_out_2));
  \var  var_11 (.in_1(in_11), .out_2(var_11_out_2));
  add add_6 (.in_1(var_11_out_2), .in_2(var_12_out_2), .out_3(add_6_out_3));
  \var  var_12 (.in_1(in_12), .out_2(var_12_out_2));
  \var  var_13 (.in_1(in_13), .out_2(var_13_out_2));
  add add_7 (.in_1(var_13_out_2), .in_2(var_14_out_2), .out_3(add_7_out_3));
  \var  var_14 (.in_1(in_14), .out_2(var_14_out_2));
  \var  var_15 (.in_1(in_15), .out_2(var_15_out_2));
  add add_8 (.in_1(var_15_out_2), .in_2(var_16_out_2), .out_3(add_8_out_3));
  \var  var_16 (.in_1(in_16), .out_2(var_16_out_2));
  dbg dbg_1 (.in_1(add_9_out_3), .out_2(dbg_1_out_2));
  add add_9 (.in_1(add_1_out_3), .in_2(add_2_out_3), .out_3(add_9_out_3));
  add add_10 (.in_1(add_9_out_3), .in_2(add_11_out_3), .out_3(add_10_out_3));
  add add_11 (.in_1(add_3_out_3), .in_2(add_4_out_3), .out_3(add_11_out_3));
  add add_12 (.in_1(add_5_out_3), .in_2(add_6_out_3), .out_3(add_12_out_3));
  add add_13 (.in_1(add_12_out_3), .in_2(add_14_out_3), .out_3(add_13_out_3));
  add add_14 (.in_1(add_7_out_3), .in_2(add_8_out_3), .out_3(add_14_out_3));
  // Probe on dbg_1_out_2
  // Probe on dbg_2_out_2
  dbg dbg_2 (.in_1(add_10_out_3), .out_2(dbg_2_out_2));
  add add_15 (.in_1(add_10_out_3), .in_2(add_13_out_3), .out_3(add_15_out_3));
  dbg dbg_3 (.in_1(add_15_out_3), .out_2(out_17));
  dbg dbg_4 (.in_1(add_13_out_3), .out_2(dbg_4_out_2));
  // Probe on dbg_4_out_2
  // Probe on out_17
endmodule

module adders (
);

  wire [7:0] superadder_1_out_17;

  // Probe on superadder_1_out_17
  superadder superadder_1 (
    .in_1(8'h1), .in_2({8{1'b0}}), .in_3({8{1'b0}}), .in_4({8{1'b0}}), .in_5({8{1'b0}}), .in_6({8{1'b0}}),
    .in_7({8{1'b0}}), .in_8({8{1'b0}}), .in_9({8{1'b0}}), .in_10({8{1'b0}}), .in_11({8{1'b0}}),
    .in_12({8{1'b0}}), .in_13({8{1'b0}}), .in_14({8{1'b0}}), .in_15({8{1'b0}}), .in_16(superadder_1_out_17),
    .out_17(superadder_1_out_17));
endmodule

module mul (
  input  A,
  input  B,
  output out_3
);

  wire add_1_out_3, add_2_out_3, add_3_out_3, add_4_out_3, add_5_out_3, add_7_out_3, and_1_out, and_2_out,
       and_3_out, and_4_out, and_5_out, and_6_out, and_7_out, and_8_out, and_9_out, and_10_out, and_11_out,
       and_12_out, and_13_out, and_14_out, and_15_out, and_16_out, clock_1_out, clock_2_out, d_ff_1_q,
       d_ff_2_q, d_ff_3_q, d_ff_4_q, d_ff_5_q, d_ff_6_q, d_ff_7_q, d_ff_8_q, d_ff_9_q, d_ff_10_q, d_ff_11_q,
       d_ff_12_q, d_ff_13_q, d_ff_14_q, d_ff_15_q, d_ff_16_q, multiplexer_1_out, multiplexer_2_out,
       multiplexer_3_out, multiplexer_4_out, multiplexer_5_out, multiplexer_6_out, multiplexer_7_out,
       multiplexer_8_out;
  wire [2:0] counter_1_q;

  Counter #(.width(3), .max('h7)) counter_1 (.Q(counter_1_q), .clk(clock_1_out));  // open: load, D, count, carry, clr
  Clock clock_1 (.out(clock_1_out));
  and and_1 (and_1_out, counter_1_q[0], ~counter_1_q[1], ~counter_1_q[2]);  // AND_Gate
  and and_2 (and_2_out, ~counter_1_q[0], counter_1_q[1], ~counter_1_q[2]);  // AND_Gate
  and and_3 (and_3_out, counter_1_q[0], counter_1_q[1], ~counter_1_q[2]);  // AND_Gate
  and and_4 (and_4_out, ~counter_1_q[0], ~counter_1_q[1], counter_1_q[2]);  // AND_Gate
  and and_5 (and_5_out, counter_1_q[0], ~counter_1_q[1], counter_1_q[2]);  // AND_Gate
  and and_6 (and_6_out, ~counter_1_q[0], counter_1_q[1], counter_1_q[2]);  // AND_Gate
  and and_7 (and_7_out, counter_1_q[0], counter_1_q[1], counter_1_q[2]);
  and and_8 (and_8_out, ~counter_1_q[0], ~counter_1_q[1], ~counter_1_q[2]);  // AND_Gate
  Clock clock_2 (.out(clock_2_out));
  Multiplexer #(.disabled(0), .enable("false")) multiplexer_1 (
    .in0(d_ff_1_q), .in1(A), .out(multiplexer_1_out), .sel(and_1_out));
  Multiplexer #(.disabled(0), .enable("false")) multiplexer_2 (
    .in0(d_ff_2_q), .in1(A), .out(multiplexer_2_out), .sel(and_2_out));
  Multiplexer #(.disabled(0), .enable("false")) multiplexer_3 (
    .in0(d_ff_3_q), .in1(A), .out(multiplexer_3_out), .sel(and_3_out));
  Multiplexer #(.disabled(0), .enable("false")) multiplexer_4 (
    .in0(d_ff_4_q), .in1(A), .out(multiplexer_4_out), .sel(and_4_out));
  Multiplexer #(.disabled(0), .enable("false")) multiplexer_5 (
    .in0(d_ff_5_q), .in1(A), .out(multiplexer_5_out), .sel(and_5_out));
  Multiplexer #(.disabled(0), .enable("false")) multiplexer_6 (
    .in0(d_ff_6_q), .in1(A), .out(multiplexer_6_out), .sel(and_6_out));
  Multiplexer #(.disabled(0), .enable("false")) multiplexer_7 (
    .in0(d_ff_7_q), .in1(A), .out(multiplexer_7_out), .sel(and_7_out));
  Multiplexer #(.disabled(0), .enable("false")) multiplexer_8 (
    .in0(d_ff_8_q), .in1(A), .out(multiplexer_8_out), .sel(and_8_out));
  D_Flip_Flop d_ff_1 (.clk(clock_2_out), .D(multiplexer_1_out), .Q(d_ff_1_q));  // open: Qn, preset, en, reset
  D_Flip_Flop d_ff_2 (.clk(clock_2_out), .D(multiplexer_2_out), .Q(d_ff_2_q));  // open: Qn, preset, en, reset
  D_Flip_Flop d_ff_3 (.clk(clock_2_out), .D(multiplexer_3_out), .Q(d_ff_3_q));  // open: Qn, preset, en, reset
  D_Flip_Flop d_ff_4 (.clk(clock_2_out), .D(multiplexer_4_out), .Q(d_ff_4_q));  // open: Qn, preset, en, reset
  D_Flip_Flop d_ff_5 (.clk(clock_2_out), .D(multiplexer_5_out), .Q(d_ff_5_q));  // open: Qn, preset, en, reset
  D_Flip_Flop d_ff_6 (.clk(clock_2_out), .D(multiplexer_6_out), .Q(d_ff_6_q));  // open: Qn, preset, en, reset
  D_Flip_Flop d_ff_7 (.clk(clock_2_out), .D(multiplexer_7_out), .Q(d_ff_7_q));  // open: Qn, preset, en, reset
  D_Flip_Flop d_ff_8 (.clk(clock_2_out), .D(multiplexer_8_out), .Q(d_ff_8_q));  // open: Qn, preset, en, reset
  D_Flip_Flop d_ff_9 (.clk(clock_2_out), .D(B), .Q(d_ff_9_q));  // open: Qn, preset, en, reset
  D_Flip_Flop d_ff_10 (.clk(clock_2_out), .D(d_ff_9_q), .Q(d_ff_10_q));  // open: Qn, preset, en, reset
  D_Flip_Flop d_ff_11 (.clk(clock_2_out), .D(d_ff_10_q), .Q(d_ff_11_q));  // open: Qn, preset, en, reset
  D_Flip_Flop d_ff_12 (.clk(clock_2_out), .D(d_ff_11_q), .Q(d_ff_12_q));  // open: Qn, preset, en, reset
  D_Flip_Flop d_ff_13 (.clk(clock_2_out), .D(d_ff_12_q), .Q(d_ff_13_q));  // open: Qn, preset, en, reset
  D_Flip_Flop d_ff_14 (.clk(clock_2_out), .D(d_ff_13_q), .Q(d_ff_14_q));  // open: Qn, preset, en, reset
  D_Flip_Flop d_ff_15 (.clk(clock_2_out), .D(d_ff_14_q), .Q(d_ff_15_q));  // open: Qn, preset, en, reset
  D_Flip_Flop d_ff_16 (.clk(clock_2_out), .D(d_ff_15_q), .Q(d_ff_16_q));  // open: Qn, preset, en, reset
  and and_9 (and_9_out, d_ff_1_q, d_ff_9_q);
  add add_1 (.in_1(and_9_out), .in_2(and_10_out), .out_3(add_1_out_3));
  and and_10 (and_10_out, d_ff_2_q, d_ff_10_q);
  and and_11 (and_11_out, d_ff_3_q, d_ff_11_q);
  add add_2 (.in_1(and_11_out), .in_2(and_12_out), .out_3(add_2_out_3));
  and and_12 (and_12_out, d_ff_4_q, d_ff_12_q);
  and and_13 (and_13_out, d_ff_5_q, d_ff_13_q);
  add add_3 (.in_1(and_13_out), .in_2(and_14_out), .out_3(add_3_out_3));
  and and_14 (and_14_out, d_ff_6_q, d_ff_14_q);
  and and_15 (and_15_out, d_ff_7_q, d_ff_15_q);
  add add_4 (.in_1(and_15_out), .in_2(and_16_out), .out_3(add_4_out_3));
  and and_16 (and_16_out, d_ff_8_q, d_ff_16_q);
  add add_5 (.in_1(add_1_out_3), .in_2(add_2_out_3), .out_3(add_5_out_3));
  add add_6 (.in_1(add_5_out_3), .in_2(add_7_out_3), .out_3(out_3));
  add add_7 (.in_1(add_3_out_3), .in_2(add_4_out_3), .out_3(add_7_out_3));
endmodule
